# Fritzing sketch moisture (saved by Fritzing 0.9.5d)
breadboards: 1

parts:
  Part1 = Arduino Mega 2560 (Rev3)
  Part2 = FC-28 Soil Hygrometer Module - Probe
  Part3 = FC-28 Soil Hygrometer Module
  OLED1 = OLED 128x64 I2C Monochrome Display
  Mod1 = KY-019 5V Relay Module [package="Breakout board"]

nets:
  N1: Part1.A0, Part3.AO
  N2: Part1.D21/SCL, OLED1.SCK
  N3: Part1.D20/SDA, OLED1.SDA
  5V: Part1.5V, Part3.VCC, OLED1.VDD, Mod1.+
  GND: Part1.GND, Part3.GND, OLED1.GND, Mod1.-
  N4: Part1.D51, Mod1.S
  N5: Part2.POS, Part3.NEG
  N6: Part2.NEG, Part3.POS

custom parts:
  FC-28 Soil Hygrometer Module - Probe: The FC-28 is a soil hygrometer module that uses the Texas Instruments LM393 comparator chip to provide an analog measurement of soil humidity.
  FC-28 Soil Hygrometer Module: The FC-28 is a soil hygrometer module that uses the Texas Instruments LM393 comparator chip to provide an analog measurement of soil humidity. The digital output is high when soil moisture is over a certain threshold, as determined by adjusting the potentiometer.
  KY-019 5V Relay Module: KY-019 5V Relay module, used to control AC circuits. (Special thanks to vanepp for fixing the PCB holes and other errors)
